# Fritzing sketch button wiring (saved by Fritzing 0.9.3b)
breadboards: 1

parts:
  WeMos_D1_Mini1 = WeMos D1 Mini
  Grove1 = Grove OLED 128x96
  S2 = Round Pushbutton
  S3 = Round Pushbutton
  S4 = Round Pushbutton
  RE2 = KY-040 Rotary encoder [package=THT]
  LED1 = smd LED [color="Red (633nm)" package="0603 [SMD]"]
  LED2 = smd LED [color="Green (570nm)" package="0603 [SMD]"]
  R1 = Resistor [tolerance=±5% resistance=220 package="2010 [SMD]"]
  R2 = Resistor [tolerance=±5% resistance=220 package="2010 [SMD]"]

nets:
  N1: WeMos_D1_Mini1.D0, S3.leg0
  N2: WeMos_D1_Mini1.D1, Grove1.SCL
  N3: WeMos_D1_Mini1.D2, Grove1.SDA
  N4: WeMos_D1_Mini1.D3, R2.Pin_1
  N5: WeMos_D1_Mini1.D4, R1.Pin_1
  N6: WeMos_D1_Mini1.D5, S4.leg0
  N7: WeMos_D1_Mini1.D6, RE2.CLK
  N8: WeMos_D1_Mini1.D7, RE2.DT
  N9: WeMos_D1_Mini1.D8, S2.leg0
  N10: WeMos_D1_Mini1.RX, RE2.SW
  GND: Grove1.GND, S2.leg1, S3.leg1, S4.leg1, RE2.GND, LED1.cathode, LED2.cathode
  VCC: Grove1.VCC, RE2.Vcc
  N11: LED1.anode, R1.Pin_0
  N12: LED2.anode, R2.Pin_0

custom parts:
  KY-040 Rotary encoder: KY-040 Rotary Encoder with switch on breakout borad from AZ Delivery
